// Logisim project Boolesche Algebra FIAE C.circ as structural Verilog: 1 circuit, main circuit main
module main (
  input  B,
  input  A,
  input  B_2,
  input  A_2,
  input  B_3,
  input  A_3,
  input  B_4,
  input  A_4,
  input  C,
  input  B_5,
  input  A_5,
  input  C_2,
  input  B_6,
  input  A_6,
  input  A_7,
  input  A_8,
  input  A_9,
  input  A_10,
  input  A_11,
  output out_20,
  output out_21,
  output out_22,
  output out_23,
  output A_v_B,
  output A___B,
  output out_26,
  output out_27,
  output A___B_2,
  output A_v_B_2,
  output B___A,
  output B_v_A,
  output out_32,
  output out_33,
  output B____C____A,
  output B__v_C__v_A,
  output A___A,
  output A_v_A,
  output A_12,
  output A_13,
  output A_v_0,
  output A___1,
  output A_14,
  output A_15,
  output out_44,
  output A_16,
  output _0___1
);

  wire and_1_out, and_4_out, and_5_out, not_1_out, not_2_out, not_4_out, not_7_out, not_8_out, undriven;

  not not_1 (not_1_out, A);
  not not_2 (not_2_out, B);
  nand nand_1 (out_20, A, B);
  and and_1 (and_1_out, A, B);
  not not_3 (out_22, and_1_out);
  or or_1 (A_v_B, not_1_out, not_2_out);
  or or_2 (out_26, ~A, ~B);  // OR_Gate
  and and_2 (A___B_2, A_3, B_3);
  and and_3 (B___A, B_3, A_3);
  and and_4 (and_4_out, A_5, B_5);
  and and_5 (and_5_out, B_5, C);
  and and_6 (A___A, A_7, A_7);
  and and_7 (A___1, A_9, 1'b1);
  and and_8 (out_32, and_4_out, C);
  and and_9 (B____C____A, A_5, and_5_out);
  not not_4 (not_4_out, A_11);
  not not_5 (out_44, not_4_out);
  not not_6 (_0___1, 1'b0);
  not not_7 (not_7_out, A_2);
  not not_8 (not_8_out, B_2);
  not not_9 (out_23, undriven);

  assign A_12 = A_7;
  assign A_15 = A_9;
  assign A_16 = A_11;

  // Notes on the sheet:
  //   NAND
  //   A
  //   B
  //   AND
  //   A
  //   NOT
  //   OR
  //   A
  //   NOT
  //   B
  //   A
  //   B
  //   B
  //   A
  //   A
  //   B
  //   B
  //   C
  //   NOT
  //   C
  //   A
  //   Boolesche Algebra
  //   De Morgansche Gesetze
  //   A ^ B
  //   =
  //   _    _
  //   Kommutativgesetz
  //   =
  //   Assoziativgesetz
  //   Idempotenzgesetz
  //   =
  //   Neutralitätsgesetz
  //   =
  //   Dualitätsgesetz
  //   (A ^ B) ^ C
  //   Doppelnegationsgesetz
  //   =
  //   A
  //   B
  //   A
  //   NOT
  //   A
  //   NOT
  //   B
  //   A
  //   B
  //   B
  //   A
  //   B
  //   C
  //   A
  //   _
  //   NOR
  //   OR
  //   AND
  //   A
  //   B
  //   C
  //   A
  //   NOT
  //   =
  //   =
  //   A v B
  //   _    _
  //   (A v B) v C
  //   =
  //   =
endmodule
